# Fritzing sketch cycleleds (saved by Fritzing 0.9.2b)
breadboards: 1

parts:
  Componente1 = Arduino Uno (Rev3)
  LED1 = LED - 5mm [color="Red (633nm)" package="5 mm [THT]"]
  R1 = Resistor [tolerance=±5% resistance=250 package=THT]
  R2 = Resistor [tolerance=±5% resistance=250 package=THT]
  R3 = Resistor [tolerance=±5% resistance=250 package=THT]
  R4 = Resistor [tolerance=±5% resistance=250 package=THT]
  R5 = Resistor [tolerance=±5% resistance=250 package=THT]
  LED2 = LED - 5mm [color="Red (633nm)" package="5 mm [THT]"]
  LED3 = LED - 5mm [color="Red (633nm)" package="5 mm [THT]"]
  LED4 = LED - 5mm [color="Red (633nm)" package="5 mm [THT]"]
  LED5 = LED - 5mm [color="Red (633nm)" package="5 mm [THT]"]

nets:
  N1: Componente1.D9_PWM, R5.Pin_1
  N2: Componente1.D10_PWM/SS, R4.Pin_1
  N3: Componente1.D11_PWM/MOSI, R3.Pin_1
  N4: Componente1.D12/MISO, R2.Pin_1
  N5: Componente1.D13/SCK, R1.Pin_1
  N6: Componente1.GND, LED1.cathode, LED2.cathode, LED3.cathode, LED4.cathode, LED5.cathode
  N7: LED1.anode, R1.Pin_0
  N8: R2.Pin_0, LED2.anode
  N9: R3.Pin_0, LED3.anode
  N10: R4.Pin_0, LED4.anode
  N11: R5.Pin_0, LED5.anode

// code stored in the sketch: cycleleds.ino
/*
 * Copyright 2015 Oto Soares Coelho Junior
 
 * Licensed under the Apache License, Version 2.0 (the "License");
 * you may not use this file except in compliance with the License.
 * You may obtain a copy of the License at
 *
 * http://www.apache.org/licenses/LICENSE-2.0
 *
 * Unless required by applicable law or agreed to in writing, software
 * distributed under the License is distributed on an "AS IS" BASIS,
 * WITHOUT WARRANTIES OR CONDITIONS OF ANY KIND, either express or implied.
 * See the License for the specific language governing permissions and
 * limitations under the License.
 * 
 * --- CYCLE LEDS: ---
 * Author: Oto Soares Coelho Junior
 * Date: 11/06/2015
 * Description: Cycles a pre-defined series of leds to forward or backward 
 * direction in determined delay time between leds.
 */

// Constants
const int LEDS_QUANTITY = 5;
const int DELAY_TIME = 500;
const int FIRST_PIN = 13;
const bool BACK_CYCLE_DIRECTION = true;

// variables (components)
int leds[LEDS_QUANTITY];

/**
 * Default Arduino setup function.
 */
void setup() {
    int pin = FIRST_PIN;
    for (int i = 0; i < LEDS_QUANTITY; i++) {
        leds[i] = pin--;
        pinMode(leds[i], OUTPUT);
    }
}

/**
 * Default Arduino loop function.
 */
void loop() {
    // Forward cycle
    for (int i = 0; i < LEDS_QUANTITY; i++) {
        onlyLedOn(i);
        delay(DELAY_TIME);
    }
    
    // Back cycle
    if (BACK_CYCLE_DIRECTION) {
        for (int i = (LEDS_QUANTITY-2); i > 0; i--) {
            onlyLedOn(i);
            delay(DELAY_TIME);
        }
    }
}

/**
 * Turns on only one led.
 * @param ledIndex: Led index.
 */
void onlyLedOn(int ledIndex) {
    for (int i = 0; i < LEDS_QUANTITY; i++)
        digitalWrite(leds[i], LOW);
    digitalWrite(leds[ledIndex], HIGH);
}
